# Fritzing sketch Proyecto (saved by Fritzing 1.0.2b)
breadboards: 1

parts:
  A1 = AHT10 module  # not connected
  A2 = ENS160 AHT21
  Capacitive_Soil_Moisture_Sensor1 = DFRobot Capacitive Soil Moisture Sensor V1.0 [part_number=SEN0193]
  U1 = 2-Channel 5v Relay Shield [package=relay-2ch5v10a]  # not connected
  WATER_PUMP1 = water pump/motor  # not connected
  Water_Level_Sensor1 = Water Level Sensor
  U2 = ESP8266 NodeMCU LoLin module  # not connected
  F1 = Fan - 4 wire [package=THT]  # not connected
  F2 = Fan - 4 wire [package=THT]  # not connected
  A3 = Micro SD card reader  # not connected
  LED1 = RGB LED (com. cathode, rgb) [color="Red (633nm)" current=0.030A package="5 mm [THT]"]  # not connected
  Componente1 = VEML7700 [part_number="Adafruit #4162"]
  A4 = AHT10 module  # not connected
  U3 = ESP8266 NodeMCU LoLin module  # not connected
  U5 = ESP8266 NodeMCU LoLin module
  VCC1 = Battery

nets:
  N1: A2.Pin_4, A2.Pin_5
  N2: Capacitive_Soil_Moisture_Sensor1.A, U5.D7
  N3: Water_Level_Sensor1.SIG, U5.D8
  VIN: Componente1.VIN, U5.3V3
  GND: Componente1.GND, U5.GND, VCC1.-
  N4: Componente1.SCL, Componente1.SDA
  N5: U5.D1, U5.D2
  N6: U5.Vin, VCC1.+

custom parts:
  AHT10 module: AHT10 Temperature Humidity Sensor Measurement Module High-Precision Digital Temp Humidity Sensor Measurement Module 1.8-6.0V I2C.
  ENS160 AHT21: The CO2 Gas- Air- Sensor is based on ENS160 in combination with an AHT21 Temperature Humidity Sensor.
  DFRobot Capacitive Soil Moisture Sensor V1.0: DFRobot Capacitive Soil Moisture Sensor V1.0 This product measures soil moisture levels by capacitive sensing, rather than resistive sensing like other types of moisture sensor. It is made of a corrosion resistant material giving it a long service life. Insert it into soil and impress your friends with the real-time soil moisture data! The product includes an on-board voltage regulator which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
  2-Channel 5v Relay Shield: 2 Channel 5v Relay Shield w. 2x SPD-06VDC-SD-C
  water pump/motor: WATER PUMP BY ARDUBLOCKTR
  Water Level Sensor: A water level sensor. This sensor operates at 3V to 5V. The Sig (signal) pin outputs an analogue signal that is in proportion to the amount of water in contact with the sensor.
  ESP8266 NodeMCU LoLin module: ESP8266 based NodeMCU
  Fan - 4 wire: Fan, 4 wire with tach.
  Micro SD card reader: Micro SD card reader.
